// Logisim project CPU.circ as structural Verilog: 1 circuit, main circuit main
module main (
  input  Reset,
  output [15:0] out_2,
  output Zero,
  output [15:0] out_4,
  output [2:0] out_5
);

  wire Beq_out, CLK_out, main_1_alu_src, main_1_branch, main_1_mem_read, main_1_mem_write, main_1_memtoreg,
       main_1_regdst, main_1_regwrite;
  wire [1:0] main_1_aluop;
  wire [2:0] multiplexer_1_out;
  wire [3:0] rom_1_data_2;
  wire [11:0] rom_1_data;
  wire [15:0] adder_1_out, adder_2_out, bit_extender_1_out, main_2_read_data_1, multiplexer_2_out,
       multiplexer_3_out, n16_bit_alu_1_result, PC_q, ram_1_data;

  Register #(.width(16)) PC (.D(multiplexer_3_out), .Q(PC_q), .clk(CLK_out), .clr(Reset));  // open: en
  Clock CLK (.out(CLK_out));
  Adder #(.width(16)) adder_1 (.a(PC_q), .b(16'h1), .out(adder_1_out));  // open: cin, cout
  ROM #(.addrWidth(16), .dataWidth(16)) rom_1 (.addr(PC_q), .data({rom_1_data_2, rom_1_data}));  // open: sel
  Control_unit_main main_1 (
    .in_1(rom_1_data_2), .RegDst(main_1_regdst), .RegWrite(main_1_regwrite), .ALU_SRC(main_1_alu_src),
    .Mem_Read(main_1_mem_read), .Mem_Write(main_1_mem_write), .MemToReg(main_1_memtoreg),
    .Branch(main_1_branch), .AlUOp(main_1_aluop));  // open: Jump
  Multiplexer #(.width(3)) multiplexer_1 (
    .in0(rom_1_data[8:6]), .in1(rom_1_data[5:3]), .out(multiplexer_1_out), .sel(main_1_regdst));  // open: en
  assign bit_extender_1_out = {{10{rom_1_data[2]}}, {rom_1_data[2:0], rom_1_data[5:3]}};  // Bit_Extender bit_extender_1
  Register_file_main main_2 (
    .WriteData(out_4), .Write_Register(multiplexer_1_out), .RegWrite(main_1_regwrite),
    .Read_data_1(main_2_read_data_1), .Read_register_1__rs(rom_1_data[11:9]), .Read_data_2(out_2),
    .Read_register_2__rt(rom_1_data[8:6]), .clk(CLK_out));
  Adder #(.width(16)) adder_2 (.a(adder_1_out), .b(bit_extender_1_out), .out(adder_2_out));  // open: cin, cout
  Multiplexer #(.width(16)) multiplexer_2 (
    .in0(out_2), .in1(bit_extender_1_out), .out(multiplexer_2_out), .sel(main_1_alu_src));  // open: en
  ALU_Control_Unit_main main_3 (.out_3(out_5), .ALUOp(main_1_aluop), .Funct(rom_1_data[2:0]));
  Multiplexer #(.width(16)) multiplexer_3 (
    .in0(adder_1_out), .in1(adder_2_out), .out(multiplexer_3_out), .sel(Beq_out));  // open: en
  and Beq (Beq_out, main_1_branch, Zero);
  _16_bit_alu u_16_bit_alu_1 (
    .B(multiplexer_2_out), .A(main_2_read_data_1), .ALU_Op(out_5[1:0]), .result(n16_bit_alu_1_result),
    .zero(Zero), .B_Inv(out_5[2]), .Cin(out_5[2]));  // open: Overflow
  RAM #(.addrWidth(16), .dataWidth(16), .bus("separate")) ram_1 (
    .addr(n16_bit_alu_1_result), .din(out_2), .data(ram_1_data), .str(main_1_mem_write), .clk(CLK_out),
    .ld(main_1_mem_read));  // open: sel, clr
  Multiplexer #(.width(16)) multiplexer_4 (
    .in0(n16_bit_alu_1_result), .in1(ram_1_data), .out(out_4), .sel(main_1_memtoreg));  // open: en

  // Notes on the sheet:
  //   I-Format
endmodule
